# Fritzing sketch Linear Actuator ICEStick (saved by Fritzing 0.9.6b)
breadboards: 1

parts:
  Bauteil1 = Lattice iCEstick
  Bauteil2 = TXB0108 8-channel Bi-directional Logic Level Converter
  Driver1 = 28BYJ-48 Driver Module [part_number=ULN2003 package=THT]
  SM1 = 28BYJ-48 Stepper Motor [part_number=28BYJ-48]
  D2F1 = D2F-FL Omron Snap Action Limit Switch with Level
  D2F2 = D2F-FL Omron Snap Action Limit Switch with Level
  S1 = Momentary Switch [package=ksa_sealed_tac_switch]

nets:
  GND: Bauteil1.GND, Bauteil2.GND, D2F1.NO, D2F2.NO, S1.3
  N1: Bauteil1.3V3, Bauteil2.OE, Bauteil2.VCCA
  N2: Bauteil1.112, Bauteil2.A4
  N3: Bauteil1.113, Bauteil2.A3
  N4: Bauteil1.114, Bauteil2.A2
  N5: Bauteil1.115, Bauteil2.A1
  N6: Bauteil1.116, D2F2.COM
  N7: Bauteil1.117, D2F1.COM
  N8: Bauteil1.118, S1.1
  N9: Bauteil2.B1, Driver1.IN1
  N10: Bauteil2.B2, Driver1.IN2
  N11: Bauteil2.B3, Driver1.IN3
  N12: Bauteil2.B4, Driver1.IN4
  N13: Driver1.blue-pin, SM1.blue-pin
  N14: Driver1.pink-pin, SM1.pink-pin
  N15: Driver1.yellow-pin, SM1.yellow-pin
  N16: Driver1.orange-pin, SM1.orange-pin
  N17: Driver1.red-pin, SM1.red-pin

notes:
  Open position
  Close position

custom parts:
  TXB0108 8-channel Bi-directional Logic Level Converter: Because the Arduino (and Basic Stamp) are 5V devices, and most modern sensors, displays, flash cards and modes are 3.3V-only, many makers find that they need to perform level shifting/conversion to protect the 3.3V device from 5V. Although one can use resistors to make a divider, for high speed transfers, the resistors can add a lot of slew and cause havoc that is tough to debug. For that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
  28BYJ-48 Driver Module: Generic male header
  28BYJ-48 Stepper Motor: Unipolar Stepper Motor 28BYJ-48 Top coil - pink & orange Bottom coil - blue & yellow Common rail - red Connector pins: blue - pink - yellow - orange - red
  D2F-FL Omron Snap Action Limit Switch with Level: Snap action switch with stainless steel lever.
