# Fritzing sketch SphericalManipulator ICEStick (saved by Fritzing 0.9.6b)
breadboards: 1

parts:
  Bauteil1 = Lattice iCEstick
  Bauteil2 = TXB0108 8-channel Bi-directional Logic Level Converter
  SERVO1 = Tower Pro SG90 servo [part_number=101246]
  SERVO2 = Tower Pro SG90 servo [part_number=101246]
  SERVO3 = Tower Pro SG90 servo [part_number=101246]

nets:
  GND: Bauteil1.GND, Bauteil2.GND, SERVO1.GND, SERVO2.GND, SERVO3.GND
  N1: Bauteil1.3V3, Bauteil2.OE, Bauteil2.VCCA
  N2: Bauteil1.113, Bauteil2.A3
  N3: Bauteil1.114, Bauteil2.A2
  N4: Bauteil1.115, Bauteil2.A1
  +5V: Bauteil2.VCCB, SERVO1.+5V, SERVO2.+5V, SERVO3.+5V
  N5: Bauteil2.B1, SERVO1.Signal
  N6: Bauteil2.B2, SERVO3.Signal
  N7: Bauteil2.B3, SERVO2.Signal

notes:
  Top
  Bottom
  Middle

custom parts:
  TXB0108 8-channel Bi-directional Logic Level Converter: Because the Arduino (and Basic Stamp) are 5V devices, and most modern sensors, displays, flash cards and modes are 3.3V-only, many makers find that they need to perform level shifting/conversion to protect the 3.3V device from 5V. Although one can use resistors to make a divider, for high speed transfers, the resistors can add a lot of slew and cause havoc that is tough to debug. For that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
  Tower Pro SG90 servo: Original file by John De Cristofaro http://www.adafruit.com/products/1449 Adafruit Feedback Servo (Small) Edited by: e-radionica.com 28/9/2015
